# Fritzing sketch DroneFritzing (saved by Fritzing 0.9.3b)

parts:
  920KV_Motor1 = DJI 920 KV Motor
  M1 = ESC
  Part1 = PocketBeagle
  Part2 = JeePlug experimenter's board
  Power_plug1 = Power plug  # not connected
  M2 = ESC
  920KV_Motor2 = DJI 920 KV Motor
  M3 = ESC
  920KV_Motor3 = DJI 920 KV Motor
  M4 = ESC
  920KV_Motor4 = DJI 920 KV Motor
  J1 = Dagu DGServo 9g header (male) [package=THT]
  J2 = Dagu DGServo 9g header (male) [package=THT]
  J3 = Dagu DGServo 9g header (male) [package=THT]
  J4 = Dagu DGServo 9g header (male) [package=THT]

nets:
  N1: 920KV_Motor1.w, M1.W
  N2: 920KV_Motor1.v, M1.V
  N3: 920KV_Motor1.u, M1.U
  N4: M1.DATA, Part1.PRU0.1, Part2.N$40, J4.gnd
  GND: M1.GND, Part1.GND, Part2.N$18, Part2.N$42, M4.GND, J1.pulse, J4.pulse
  N5: Part1.PWM0A, Part2.N$32, M2.DATA, J3.gnd
  N6: Part1.PWM1A, Part2.N$25, M3.DATA, J2.gnd
  N7: Part1.GPIO23, Part2.N$16, M4.DATA, J1.gnd
  N8: Part2.N$17, J1.Vcc
  N9: Part2.N$27, J2.Vcc
  N10: Part2.N$28, M3.GND, J2.pulse
  N11: Part2.N$33, J3.Vcc
  N12: Part2.N$34, M2.GND, J3.pulse
  N13: Part2.N$41, J4.Vcc
  N14: M2.U, 920KV_Motor2.u
  N15: M2.V, 920KV_Motor2.v
  N16: M2.W, 920KV_Motor2.w
  N17: M3.U, 920KV_Motor3.u
  N18: M3.V, 920KV_Motor3.v
  N19: M3.W, 920KV_Motor3.w
  N20: M4.U, 920KV_Motor4.u
  N21: M4.V, 920KV_Motor4.v
  N22: M4.W, 920KV_Motor4.w

notes:
  -ESCs can be 20A or 30A
  -ESC power connections omitted for brevity
  Power in -> 4s LiPo
  Yellow - P2_1
  Green - P2_3
  Orange - P1_33
  Blue - P1_36

custom parts:
  DJI 920 KV Motor: DJI Brushless Outrunner 2212/920K Motor F330-550
